// Digital circuit ALU.dig as structural Verilog
module ALU (
  input  cl,
  input  [31:0] in0,
  input  [31:0] in1,
  input  [31:0] carryin,
  input  [7:0] instr0_7,
  input  instrbit9,
  input  pushoverwrite,
  input  popoverwrite,
  input  cl_double,
  output [31:0] \output ,
  output [31:0] carry,
  output [31:0] stackeeh
);

  wire [31:0] arithmaticenginewithfloatt_1_p6, arithmaticenginewithfloatt_1_p7, logicengine_1_p4,
       shift_1_carry, shift_1_out;

  // arithmaticenginewithfloatt arithmaticenginewithfloatt_1: pin names not known; wires that end beside it: in0, in1, carryin, instr0_7, instrbit9, arithmaticenginewithfloatt_1_p6, arithmaticenginewithfloatt_1_p7
  // logicengine logicengine_1: pin names not known; wires that end beside it: in0, in1, instr0_7, logicengine_1_p4
  shift shift_1 (
    .in0(in0), .in1(in1), .carryin(carryin), .instr0_7(instr0_7), .pushoverwrite(pushoverwrite),
    .popoverwrite(popoverwrite), .cl(cl), .cl_double(cl_double), .out(shift_1_out), .carry(shift_1_carry),
    .stackeeh(stackeeh));
  Multiplexer #(.Bits(32)) multiplexer_1 (
    .sel(instr0_7[3]), .in_0(arithmaticenginewithfloatt_1_p7), .in_1(shift_1_carry), .out(carry));
  Multiplexer #(.Selector_Bits(2), .Bits(32)) multiplexer_2 (
    .sel(instr0_7[4:3]), .in_0({32{1'b0}}), .in_1(logicengine_1_p4), .in_2(arithmaticenginewithfloatt_1_p6),
    .in_3(shift_1_out), .out(\output ));
endmodule
