// Digital circuit CPU.dig as structural Verilog
module CPU (
  input  cl,
  input  [63:0] instruction,
  input  [31:0] in0,
  input  [31:0] in1,
  input  [31:0] in2,
  input  interrupt,
  output [31:0] cycles,
  output [31:0] address,
  output outputflag0,
  output [31:0] output0,
  output outputflag1,
  output [31:0] output1,
  output outputflag2,
  output [31:0] output2,
  output outputflag3,
  output [31:0] output3,
  output inputflag0,
  output inputflag1,
  output inputflag2
);

  wire comparison_1_out, counter_1_out, d_ff_1_q, decoder_1_call, decoder_1_copyptr, decoder_1_exit,
       decoder_1_hlt, decoder_1_ret_yn_2, decoder_1_save_carry, decoder_1_save_yn, multiplexer_1_out,
       multiplexer_2_out, multiplexer_3_out, not_1_out, or_1_out, register_1_q, rs_ff_as_1_q;
  wire [31:0] alu_1_output, alu_1_stackeeh, decoder_1_dst, decoder_1_value, mem_block_1_p7, mem_block_1_p16,
       mem_block_1_p17, mem_block_1_p18, mem_block_1_p19, multiplexer_4_out;

  D_FF d_ff_1 (.D(decoder_1_exit), .C(multiplexer_2_out), .Q(d_ff_1_q));  // open: nQ
  Multiplexer multiplexer_1 (.sel(d_ff_1_q), .in_0(cl), .in_1(1'b0), .out(multiplexer_1_out));
  decoder decoder_1 (
    .instr0_7(instruction[55:48]), .comparison(comparison_1_out), .ALU(alu_1_output),
    .selectdst(mem_block_1_p18), .subroutinereg(alu_1_stackeeh), .counter(address),
    .Ret_yn(decoder_1_ret_yn_2), .counter_yn(or_1_out), .instr8_15(instruction[63:56]), .dst(decoder_1_dst),
    .value(decoder_1_value), .save_yn(decoder_1_save_yn), .save_carry(decoder_1_save_carry),
    .exit(decoder_1_exit), .hlt(decoder_1_hlt), .copyptr(decoder_1_copyptr), .call(decoder_1_call),
    .ret_yn_2(decoder_1_ret_yn_2));
  Multiplexer multiplexer_2 (.sel(rs_ff_as_1_q), .in_0(multiplexer_1_out), .in_1(1'b0), .out(multiplexer_2_out));
  RS_FF_AS rs_ff_as_1 (.S(decoder_1_hlt), .R(interrupt), .Q(rs_ff_as_1_q));  // open: nQ
  Counter counter_1 (.en(1'b1), .C(~multiplexer_2_out), .clr(1'b0), .out(counter_1_out));  // open: ovf
  or or_1 (or_1_out, decoder_1_exit, decoder_1_hlt);
  not not_1 (not_1_out, counter_1_out);
  Counter #(.Bits(32)) counter_2 (.en(not_1_out), .C(not_1_out), .clr(1'b0), .out(cycles));  // open: ovf
  Multiplexer multiplexer_3 (.sel(instruction[59]), .in_0(interrupt), .in_1(1'b0), .out(multiplexer_3_out));
  // mem_block mem_block_1: pin names not known; wires that end beside it: multiplexer_2_out, not_1_out, decoder_1_dst, decoder_1_save_yn, decoder_1_value, decoder_1_save_carry, mem_block_1_p7, instruction[55:48], decoder_1_copyptr, {{16{1'b0}}, instruction[47:32]}, {{16{1'b0}}, instruction[31:16]}, {{16{1'b0}}, instruction[15:0]}, in0, in1, in2, mem_block_1_p16, mem_block_1_p17, mem_block_1_p18, mem_block_1_p19, outputflag0, output0, outputflag1, output1, outputflag2, output2, outputflag3, output3, address, inputflag0, inputflag1, inputflag2
  Register register_1 (.D(multiplexer_3_out), .C(~not_1_out), .en(1'b1), .Q(register_1_q));
  Multiplexer #(.Bits(32)) multiplexer_4 (
    .sel(decoder_1_call), .in_0(mem_block_1_p16), .in_1(address), .out(multiplexer_4_out));
  ALU alu_1 (
    .cl(not_1_out), .in0(multiplexer_4_out), .in1(mem_block_1_p17), .carryin(mem_block_1_p19),
    .instr0_7(instruction[55:48]), .instrbit9(instruction[57]), .pushoverwrite(decoder_1_call),
    .popoverwrite(decoder_1_ret_yn_2), .cl_double(multiplexer_2_out), .\output (alu_1_output),
    .carry(mem_block_1_p7), .stackeeh(alu_1_stackeeh));
  comparison comparison_1 (
    .in0(mem_block_1_p16), .in1(mem_block_1_p17), .instr0_7(instruction[55:48]), .instr8(instruction[56]),
    .instr9(instruction[57]), .instr11(instruction[59]), .interrupt(register_1_q), .out(comparison_1_out));

  // Notes on the sheet:
  //   instruction: default 49539595901140992
endmodule
