// Digital circuit comparison.dig as structural Verilog
module comparison (
  input  [31:0] in0,
  input  [31:0] in1,
  input  [7:0] instr0_7,
  input  instr8,
  input  instr9,
  input  instr11,
  input  interrupt,
  output out
);

  wire and_1_out, and_2_out, and_3_out, and_4_out, and_5_out, and_6_out, and_7_out, and_8_out, and_9_out,
       and_10_out, and_11_out, and_12_out, and_13_out, and_14_out, and_15_out, comparator_1_eq,
       comparator_1_gt, comparator_1_lt, comparator_2_eq, comparator_2_gt, comparator_2_lt, comparator_3_eq,
       comparator_3_gt, comparator_3_lt, comparator_4_eq, comparator_4_gt, comparator_4_lt, comparator_5_eq,
       comparator_5_gt, comparator_5_lt, multiplexer_1_out, multiplexer_2_out, or_1_out, or_2_out, or_3_out,
       or_4_out, or_5_out;

  Comparator #(.Signed("true"), .Bits(32)) comparator_1 (
    .a(in0), .b(in1), .gt(comparator_1_gt), .eq(comparator_1_eq), .lt(comparator_1_lt));
  Comparator #(.Bits(32)) comparator_2 (
    .a(in0), .b(in1), .gt(comparator_2_gt), .eq(comparator_2_eq), .lt(comparator_2_lt));
  and and_1 (and_1_out, instr0_7[0], comparator_1_gt);
  and and_2 (and_2_out, instr0_7[1], comparator_1_eq);
  and and_3 (and_3_out, instr0_7[2], comparator_1_lt);
  and and_4 (and_4_out, comparator_2_gt, instr0_7[0]);
  and and_5 (and_5_out, comparator_2_eq, instr0_7[1]);
  and and_6 (and_6_out, comparator_2_lt, instr0_7[2]);
  Comparator comparator_3 (.a(in0[31]), .b(in1[31]), .gt(comparator_3_gt), .eq(comparator_3_eq), .lt(comparator_3_lt));
  Comparator #(.Bits(8)) comparator_4 (
    .a(in0[30:23]), .b(in1[30:23]), .gt(comparator_4_gt), .eq(comparator_4_eq), .lt(comparator_4_lt));
  Comparator #(.Bits(23)) comparator_5 (
    .a(in0[22:0]), .b(in1[22:0]), .gt(comparator_5_gt), .eq(comparator_5_eq), .lt(comparator_5_lt));
  or or_1 (or_1_out, and_1_out, and_2_out, and_3_out);
  or or_2 (or_2_out, and_4_out, and_5_out, and_6_out);
  Multiplexer multiplexer_1 (.sel(instr8), .in_0(or_1_out), .in_1(or_2_out), .out(multiplexer_1_out));
  Multiplexer multiplexer_2 (.sel(instr9), .in_0(multiplexer_1_out), .in_1(or_5_out), .out(multiplexer_2_out));
  and and_7 (and_7_out, comparator_3_eq, comparator_4_gt);
  and and_8 (and_8_out, comparator_3_eq, comparator_4_eq, comparator_5_gt);
  and and_9 (and_9_out, comparator_4_lt, comparator_3_eq);
  and and_10 (and_10_out, comparator_5_lt, comparator_4_eq, comparator_3_eq);
  and and_11 (and_11_out, multiplexer_2_out, interrupt);
  Multiplexer multiplexer_3 (.sel(instr11), .in_0(multiplexer_2_out), .in_1(and_11_out), .out(out));
  or or_3 (or_3_out, comparator_3_lt, and_7_out, and_8_out);
  and and_12 (and_12_out, comparator_4_eq, comparator_5_eq, comparator_3_eq);
  or or_4 (or_4_out, comparator_3_gt, and_9_out, and_10_out);
  and and_13 (and_13_out, instr0_7[0], or_3_out);
  and and_14 (and_14_out, instr0_7[1], and_12_out);
  and and_15 (and_15_out, instr0_7[2], or_4_out);
  or or_5 (or_5_out, and_13_out, and_14_out, and_15_out);
endmodule
