// Digital circuit computerscreen.dig as structural Verilog
module computerscreen (
  input  clk,
  input  [31:0] in1,
  input  [31:0] in2,
  input  interrupt,
  input  [31:0] in0,
  output [31:0] out_5
);

  wire cpu_1_inputflag0, cpu_1_inputflag1, cpu_1_inputflag2, cpu_1_outputflag0, cpu_1_outputflag1,
       cpu_1_outputflag2, cpu_1_outputflag3, prng_1_r;
  wire [15:0] keyboard_1_d;
  wire [31:0] cpu_1_address, cpu_1_output0, cpu_1_output1, cpu_1_output2, cpu_1_output3, register_1_q,
       register_2_q;
  wire [63:0] rom_1_d;

  ROM #(.AddrBits(24), .Bits(64)) rom_1 (.A(cpu_1_address[23:0]), .sel(1'b1), .D(rom_1_d));
  PRNG prng_1 (.S(1'b1), .se(1'b0), .ne(1'b1), .C(clk), .R(prng_1_r));
  Keyboard keyboard_1 (.C(cpu_1_outputflag3), .en(1'b1), .D(keyboard_1_d));  // open: av
  CPU cpu_1 (
    .cl(clk), .instruction(rom_1_d), .in0(in0), .in1(in1), .in2(in2), .interrupt(interrupt),
    .address(cpu_1_address), .outputflag0(cpu_1_outputflag0), .output0(cpu_1_output0),
    .outputflag1(cpu_1_outputflag1), .output1(cpu_1_output1), .outputflag2(cpu_1_outputflag2),
    .output2(cpu_1_output2), .outputflag3(cpu_1_outputflag3), .output3(cpu_1_output3),
    .inputflag0(cpu_1_inputflag0), .inputflag1(cpu_1_inputflag1), .inputflag2(cpu_1_inputflag2));  // open: cycles
  Register #(.Bits(32)) register_1 (.D(cpu_1_output0), .C(cpu_1_outputflag0), .en(cpu_1_outputflag0), .Q(register_1_q));
  Register #(.Bits(32)) register_2 (.D(cpu_1_output2), .C(cpu_1_outputflag2), .en(cpu_1_outputflag2), .Q(register_2_q));
  Register #(.Bits(32)) register_3 (.D(cpu_1_output3), .C(cpu_1_outputflag3), .en(cpu_1_outputflag3), .Q(out_5));
  GraphicCard #(.graphicHeight(512), .graphicWidth(512), .Bits(16)) graphiccard_1 (
    .A({1'b0, cpu_1_output1[8:0], register_1_q[8:0]}), .str(1'b1), .C(cpu_1_outputflag1), .ld(1'b0),
    .B(1'b0), .D(register_2_q[15:0]));

  // Notes on the sheet:
  //   clk: Hz: 2147483647
  //   in0: default 256
  //   contents of rom_1 (hex, n*v repeats v):
  //   f0000000000000,70002000000006,f0000200000025,f0000300000026,f0002700000000
  //   ,f0000500000001,e500010001001e,f0000100000002,f0000100000005,b0002500050003
  //   ,770000300000003,35000100030007,6500230000000f,f0000000000002
  //   ,27001600000016,b0002500050003,770000300000003,34000300030003
  //   ,26000300010014,27001600000016,36000500050005,27000900000009,6500020001001a
  //   ,50000100000000,70000000010000,70000000000021,2500000006001c,27001e0000001e
  //   ,70000100020001,27000600000006,f0002500000000,770000000000007
  //   ,75000727100008,75002303e80009,7500230064000a,750023000a000b,7000230000000c
  //   ,70000800300020,70000900300020,70000a00300020,70000b00300020,70000c00300020
  //   ,f0002000000020,70000000010000,2500000006001f,600000000000000
endmodule
