// Digital circuit decoder.dig as structural Verilog
module decoder (
  input  [7:0] instr0_7,
  input  comparison,
  input  [31:0] ALU,
  input  [31:0] selectdst,
  input  [31:0] subroutinereg,
  input  [31:0] counter,
  input  Ret_yn,
  input  counter_yn,
  input  [7:0] instr8_15,
  output [31:0] dst,
  output [31:0] value,
  output save_yn,
  output save_carry,
  output exit,
  output hlt,
  output copyptr,
  output call,
  output ret_yn_2
);

  wire and_1_out, and_2_out, comparator_1_eq, multiplexer_4_out, nor_1_out;
  wire [31:0] multiplexer_1_out, multiplexer_2_out;

  Multiplexer #(.Bits(32)) multiplexer_1 (.sel(counter_yn), .in_0(selectdst), .in_1(counter), .out(multiplexer_1_out));
  Multiplexer #(.Bits(32)) multiplexer_2 (
    .sel(Ret_yn), .in_0(multiplexer_1_out), .in_1(subroutinereg), .out(multiplexer_2_out));
  nor nor_1 (nor_1_out, instr0_7[3], instr0_7[4]);
  Multiplexer #(.Bits(32)) multiplexer_3 (.sel(nor_1_out), .in_0(selectdst), .in_1(32'h24), .out(dst));
  and and_1 (and_1_out, instr0_7[4], ~instr0_7[3]);  // And
  and and_2 (and_2_out, ~instr0_7[2], instr0_7[3], instr0_7[4]);  // And
  and and_3 (exit, ~instr0_7[1], ~instr8_15[0], instr8_15[1], instr8_15[2]);  // And
  and and_4 (hlt, instr0_7[1], ~instr8_15[0], instr8_15[1], instr8_15[2]);  // And
  and and_5 (copyptr, instr8_15[0], instr8_15[1], instr8_15[2]);
  and and_6 (call, ~instr8_15[0], ~instr8_15[1], instr8_15[2]);  // And
  and and_7 (ret_yn_2, instr8_15[0], ~instr8_15[1], instr8_15[2]);  // And
  Multiplexer multiplexer_4 (.sel(nor_1_out), .in_0(1'b1), .in_1(comparison), .out(multiplexer_4_out));
  Multiplexer #(.Bits(32)) multiplexer_5 (.sel(nor_1_out), .in_0(ALU), .in_1(multiplexer_2_out), .out(value));
  or or_1 (save_carry, and_1_out, and_2_out);
  Comparator #(.Bits(7)) comparator_1 (.a(instr0_7[6:0]), .b(7'b0011111), .eq(comparator_1_eq));  // open: gt, lt
  Multiplexer multiplexer_6 (.sel(comparator_1_eq), .in_0(multiplexer_4_out), .in_1(1'b0), .out(save_yn));
endmodule
