// Digital circuit floatdiv.dig as structural Verilog
module floatdiv (
  input  [22:0] m0,
  input  [22:0] m1,
  input  [7:0] e0,
  input  [7:0] e1,
  input  s0,
  input  s1,
  output [22:0] m,
  output [7:0] e,
  output s
);

  wire [0:0] not_1_out;
  wire [7:0] add_1_s, sub_1_s;
  wire [47:0] div_1_p3;

  Sub #(.Bits(8)) sub_1 (.a(e0), .b(e1), .c_i(1'b0), .s(sub_1_s));  // open: c_o
  xor xor_1 (s, s0, s1);
  // div div_1: pin names not known; wires that end beside it: {1'b1, m0}, {1'b1, m1}, div_1_p3
  Add #(.Bits(8)) add_1 (.a(8'h7f), .b(sub_1_s), .c_i(1'b0), .s(add_1_s));  // open: c_o
  not not_1 (not_1_out[0], div_1_p3[24]);
  Sub #(.Bits(8)) sub_2 (.a(add_1_s), .b({8{1'b0}}), .c_i(not_1_out[0]), .s(e));  // open: c_o
  BarrelShifter #(.Bits(23)) barrelshifter_1 (.in(div_1_p3[23:1]), .shift({4'b0000, not_1_out[0]}), .out(m));

  // Notes on the sheet:
  //   e0: default 128
  //   e1: default 129
endmodule
