// Digital circuit shift.dig as structural Verilog
module shift (
  input  [31:0] in0,
  input  [31:0] in1,
  input  [31:0] carryin,
  input  [7:0] instr0_7,
  input  pushoverwrite,
  input  popoverwrite,
  input  cl,
  input  cl_double,
  output [31:0] out,
  output [31:0] carry,
  output [31:0] stackeeh
);

  wire comparator_1_eq, comparator_2_eq, or_1_out, or_2_out;
  wire [6:0] add_1_s, add_2_s, not_1_out, not_2_out;
  wire [31:0] add_3_s, barrelshifter_5_out, barrelshifter_6_out, driver_1_out;
  wire [63:0] barrelshifter_1_out, barrelshifter_2_out, barrelshifter_3_out, barrelshifter_4_out;

  assign driver_1_out = instr0_7[0] ? carryin : 32'bz;  // Driver driver_1
  PullDown #(.Bits(32)) pulldown_1 (.out(driver_1_out));
  Comparator #(.Bits(7)) comparator_1 (.a(instr0_7[6:0]), .b(7'b0111111), .eq(comparator_1_eq));  // open: gt, lt
  Comparator #(.Bits(7)) comparator_2 (.a(instr0_7[6:0]), .b(7'b0011111), .eq(comparator_2_eq));  // open: gt, lt
  assign not_1_out = ~in1[6:0];  // Not not_1, 7 bits wide
  assign not_2_out = ~in1[6:0];  // Not not_2, 7 bits wide
  BarrelShifter #(.Bits(64)) barrelshifter_1 (.in({in0, driver_1_out}), .shift(in1[6:0]), .out(barrelshifter_1_out));
  Add #(.Bits(7)) add_1 (.a(not_1_out), .b(7'b1000001), .c_i(1'b0), .s(add_1_s));  // open: c_o
  BarrelShifter #(.Bits(64), .direction("right")) barrelshifter_2 (
    .in({driver_1_out, in0}), .shift(in1[6:0]), .out(barrelshifter_2_out));
  Add #(.Bits(7)) add_2 (.a(not_2_out), .b(7'b1000001), .c_i(1'b0), .s(add_2_s));  // open: c_o
  or or_1 (or_1_out, comparator_1_eq, popoverwrite);
  or or_2 (or_2_out, comparator_2_eq, pushoverwrite);
  BarrelShifter #(.Bits(64), .direction("right")) barrelshifter_3 (
    .in({in0, {32{1'b0}}}), .shift(add_1_s), .out(barrelshifter_3_out));
  BarrelShifter #(.Bits(64)) barrelshifter_4 (.in({{32{1'b0}}, in0}), .shift(add_2_s), .out(barrelshifter_4_out));
  BarrelShifter #(.Bits(32), .barrelShifterMode("rotate")) barrelshifter_5 (
    .in(in0), .shift(in1[5:0]), .out(barrelshifter_5_out));
  BarrelShifter #(.Bits(32), .barrelShifterMode("rotate"), .direction("right")) barrelshifter_6 (
    .in(in0), .shift(in1[5:0]), .out(barrelshifter_6_out));
  Add #(.Bits(32)) add_3 (.a(in0), .b({32{1'b0}}), .c_i(pushoverwrite), .s(add_3_s));  // open: c_o
  stack stack_1 (.cl(cl), .pop(or_1_out), .push(or_2_out), .value(add_3_s), .cl_double(cl_double), .out(stackeeh));
  Multiplexer #(.Selector_Bits(3), .Bits(32)) multiplexer_1 (
    .sel(instr0_7[2:0]), .in_0(barrelshifter_1_out[63:32]), .in_1(barrelshifter_1_out[63:32]),
    .in_2(barrelshifter_2_out[31:0]), .in_3(barrelshifter_2_out[31:0]), .in_4(barrelshifter_5_out),
    .in_5(barrelshifter_6_out), .in_6({carryin[15:0], in0[15:0]}), .in_7(stackeeh), .out(out));
  Multiplexer #(.Bits(32)) multiplexer_2 (
    .sel(instr0_7[1]), .in_0(barrelshifter_3_out[31:0]), .in_1(barrelshifter_4_out[63:32]), .out(carry));

  // Notes on the sheet:
  //   in0: default 2
  //   in1: default 2
endmodule
