// Digital circuit stack.dig as structural Verilog
module stack (
  input  cl,
  input  pop,
  input  push,
  input  [31:0] value,
  input  cl_double,
  output [31:0] out
);

  wire and_1_out, and_2_out, not_1_out, not_2_out, not_4_out, or_1_out;
  wire [23:0] add_1_s, multiplexer_1_out, not_3_out, register_1_q;
  wire [31:0] ramdualport_1_d;

  not not_1 (not_1_out, cl);
  and and_1 (and_1_out, not_1_out, cl_double);
  or or_1 (or_1_out, pop, push);
  not not_2 (not_2_out, and_1_out);
  and and_2 (and_2_out, not_2_out, push);
  Register #(.Bits(24)) register_1 (.D(add_1_s), .C(and_1_out), .en(or_1_out), .Q(register_1_q));
  assign not_3_out = ~24'h1;  // Not not_3, 24 bits wide
  not not_4 (not_4_out, push);
  Multiplexer #(.Bits(24)) multiplexer_1 (.sel(push), .in_0(not_3_out), .in_1(24'h1), .out(multiplexer_1_out));
  RAMDualPort #(.AddrBits(24), .Bits(32)) ramdualport_1 (
    .A(register_1_q), .Din(value), .str(push), .C(and_2_out), .ld(1'b1), .D(ramdualport_1_d));
  Add #(.Bits(24)) add_1 (.a(register_1_q), .b(multiplexer_1_out), .c_i(not_4_out), .s(add_1_s));  // open: c_o
  Register #(.Bits(32)) register_2 (.D(ramdualport_1_d), .C(and_1_out), .en(1'b1), .Q(out));

  // Notes on the sheet:
  //   value: default 2
endmodule
